// Digital circuit Mux_8_1.dig as structural Verilog
module Mux_8_1 (
  input  D7,
  input  D6,
  input  D5,
  input  D4,
  input  D3,
  input  D2,
  input  D1,
  input  D0,
  input  Sel_0,
  input  Sel_1,
  input  Sel_2,
  output out_12,
  output out_13,
  output out_14,
  output out_15,
  output out_16,
  output out_17,
  output out_18,
  output out_19
);

  wire S0_t, S1_t, S2_t;

  not not_1 (S2_t, Sel_2);
  not not_2 (S1_t, Sel_1);
  not not_3 (S0_t, Sel_0);
  and and_1 (out_12, D1, Sel_2, Sel_1, Sel_0);
  and and_2 (out_13, D1, Sel_2, Sel_1, S0_t);
  and and_3 (out_14, D1, Sel_2, S1_t, Sel_0);
  and and_4 (out_15, D4, Sel_2, S1_t, S0_t);
  and and_5 (out_16, D3, S2_t, Sel_1, Sel_0);
  and and_6 (out_17, D2, S2_t, Sel_1, S0_t);
  and and_7 (out_18, D1, S2_t, S1_t, Sel_0);
  and and_8 (out_19, D0, S2_t, S1_t, S0_t);

  // Other names for the same wires on the sheet: S0 = Sel_0; S1 = Sel_1; S2 = Sel_2
endmodule
