// Digital circuit demux_4_1.dig as structural Verilog
module demux_4_1 (
  input  D0,
  input  S0,
  input  S1,
  output O3,
  output O2,
  output O1,
  output O0
);

  wire not_1_out, not_2_out;

  not not_1 (not_1_out, S1);
  and and_1 (O3, D0, S1, S0);
  and and_2 (O2, D0, S1, not_2_out);
  and and_3 (O1, D0, not_1_out, S0);
  and and_4 (O0, D0, not_1_out, not_2_out);
  not not_2 (not_2_out, S0);
endmodule
