// Digital circuit registro4bits.dig as structural Verilog
module registro4bits (
  input  Set,
  input  D0,
  input  Clock,
  input  Clear,
  input  D1,
  input  D2,
  input  D3,
  input  in_9,
  input  in_11,
  input  in_13,
  input  in_15,
  input  Set_2,
  input  Clear_2,
  input  Set_3,
  input  Clear_3,
  input  in_24,
  input  in_25,
  input  in_26,
  input  in_27,
  output out_8,
  output out_10,
  output out_12,
  output out_14,
  output out_16,
  output out_17,
  output out_18,
  output out_19
);

  wire d_ff_as_3_q, d_ff_as_5_q, d_ff_as_7_q, d_ff_as_8_q, I0, I1, I2, I3, O0, O1, O2, O3;

  D_FF_AS d_ff_as_1 (.Set(Set_2), .D(I0), .C(Clock), .Clr(Clear_2), .Q(out_19));  // open: nQ
  D_FF_AS d_ff_as_2 (.Set(Set_2), .D(I1), .C(Clock), .Clr(Clear_2), .Q(out_18));  // open: nQ
  D_FF_AS d_ff_as_3 (.Set(Set), .D(D0), .C(Clock), .Clr(Clear), .Q(d_ff_as_3_q));  // open: nQ
  D_FF_AS d_ff_as_4 (.Set(Set_2), .D(I2), .C(Clock), .Clr(Clear_2), .Q(out_17));  // open: nQ
  assign out_8 = ~d_ff_as_3_q ? O0 : 1'bz;  // DriverInvSel driverinvsel_1
  assign I0 = d_ff_as_3_q ? in_9 : 1'bz;  // Driver driver_1
  D_FF_AS d_ff_as_5 (.Set(Set), .D(D1), .C(Clock), .Clr(Clear), .Q(d_ff_as_5_q));  // open: nQ
  assign out_10 = ~d_ff_as_5_q ? O1 : 1'bz;  // DriverInvSel driverinvsel_2
  D_FF_AS d_ff_as_6 (.Set(Set_2), .D(I3), .C(Clock), .Clr(Clear_2), .Q(out_16));  // open: nQ
  D_FF_AS d_ff_as_7 (.Set(Set), .D(D2), .C(Clock), .Clr(Clear), .Q(d_ff_as_7_q));  // open: nQ
  assign I1 = d_ff_as_5_q ? in_11 : 1'bz;  // Driver driver_2
  assign out_12 = ~d_ff_as_7_q ? O2 : 1'bz;  // DriverInvSel driverinvsel_3
  assign I2 = d_ff_as_7_q ? in_13 : 1'bz;  // Driver driver_3
  D_FF_AS d_ff_as_8 (.Set(Set), .D(D3), .C(Clock), .Clr(Clear), .Q(d_ff_as_8_q));  // open: nQ
  D_FF_AS d_ff_as_9 (.Set(Set_3), .D(in_24), .C(Clock), .Clr(Clear_3), .Q(O0));  // open: nQ
  assign out_14 = ~d_ff_as_8_q ? O3 : 1'bz;  // DriverInvSel driverinvsel_4
  assign I3 = d_ff_as_8_q ? in_15 : 1'bz;  // Driver driver_4
  D_FF_AS d_ff_as_10 (.Set(Set_3), .D(in_25), .C(Clock), .Clr(Clear_3), .Q(O1));  // open: nQ
  D_FF_AS d_ff_as_11 (.Set(Set_3), .D(in_26), .C(Clock), .Clr(Clear_3), .Q(O2));  // open: nQ
  D_FF_AS d_ff_as_12 (.Set(Set_3), .D(in_27), .C(Clock), .Clr(Clear_3), .Q(O3));  // open: nQ

  // Notes on the sheet:
  //   Almacena datos si se configura como ENTRADA
  //   Registro de configuración
  //   0 = Salida 1 = Entrada
  //   Controla los estados si se configura como SALIDA
endmodule
