// Digital circuit flipflopJK.dig as structural Verilog
module flipflopJK (
  input  J,
  input  C,
  input  K,
  output Q
);

  wire and_1_out, and_2_out, nand_1_out, nand_2_out, nand_3_out, nand_4_out, nand_5_out, nand_6_out,
       nand_8_out, not_1_out;

  and and_1 (and_1_out, nand_8_out, J);
  and and_2 (and_2_out, C, K);
  nand nand_1 (nand_1_out, and_1_out, C);
  nand nand_2 (nand_2_out, and_2_out, Q);
  not not_1 (not_1_out, C);
  nand nand_3 (nand_3_out, nand_1_out, nand_4_out);
  nand nand_4 (nand_4_out, nand_3_out, nand_2_out);
  nand nand_5 (nand_5_out, nand_3_out, not_1_out);
  nand nand_6 (nand_6_out, not_1_out, nand_4_out);
  nand nand_7 (Q, nand_5_out, nand_8_out);
  nand nand_8 (nand_8_out, Q, nand_6_out);

  // Notes on the sheet:
  //   J K Q
  //   1 0 1, establece la salida a 1(setea)
  //   0 1 0, establece la salida a 0(resetea)
  //   0 0 -> Estado de memoria, preserva el valor que tenía antes
  //   1 1 -> Estado complementario, da el inverso de la salida que se tenía antes
  //   Se hace con dos flipflop RS en cascada para evitar un comportamiento oscilatorio
  //   en la parte complementaria, esto se logra debido a la señal de reloj invertida que hay
  //   entre los dos flipflops.
  //   En el flipflop main se da el comportamiento JK y en el secondary se da la propagación y salida
  //   Main
  //   Secondary
endmodule
