// Digital circuit flipflopRS.dig as structural Verilog
module flipflopRS (
  input  in_2,
  input  clk,
  input  in_4,
  output Output
);

  wire and_1_out, and_2_out, and_3_out, and_4_out, nor_2_out;

  and and_1 (and_1_out, Output, in_4);
  and and_2 (and_2_out, clk, in_2);
  and and_3 (and_3_out, and_1_out, clk);
  and and_4 (and_4_out, and_2_out, nor_2_out);
  nor nor_1 (Output, and_3_out, nor_2_out);
  nor nor_2 (nor_2_out, Output, and_4_out);

  // Notes on the sheet:
  //   N1
  //   N2
  //   El flip-flop JK tiene 4 estados, 
  //   R S
  //   0 0 -> Memoria, guarda el último dato que se haya puesto en la salida.
  //   como siempre hay una compuerta que da salida, se mantiene el estado
  //   1 0 -> Limpiar, manda el estado de la salida a 0.
  //   como R se activa, la compuerta N1 da una salida 0
  //   0 1 -> Ajuste, permite ajustar el valor que se tendrá en la salida.
  //   se activa S entonces la compuerta N2 manda una señal de 0 a la
  //   N1, lo que hace que salida = 1 
  //   1 1 -> Complementa el estado anterior, es decir, si la salida era 0, se convierte en 1 y viceversa
endmodule
